# Fritzing sketch hidden_device (saved by Fritzing 1.0.0rc)
breadboards: 1

parts:
  part = Arduino Uno Mini LE
  FSR = Basic Force Sensing Resistor (FSR) [package=THT]
  part_2 = Resistor [tolerance=±5% power=0.25W resistance=10k part_number=R1 package=THT]

nets:
  N1: part.A0, FSR.pin_1, part_2.Pin_0
  N2: part.GND, part_2.Pin_1
  N3: part.3V3, FSR.pin_2

custom parts:
  Arduino Uno Mini LE: The UNO Mini Limited Edition (LE) is a miniature version of the classic Arduino UNO board. It is based on the ATmega328P microcontroller, has USB-C connector for programming and powering the board, and pins available for connecting external power sources. It also comes with the standard set of female pin connectors, built-in LED, reset button and everything else that the standard UNO have, but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
